// Logisim project Full Subtractor.circ as structural Verilog: 1 circuit, main circuit main
module main (
  input  in_1,
  input  in_2,
  input  in_3,
  input  in_4,
  input  in_5
);

  wire and_1_out, and_2_out, not_1_out, not_2_out, undriven;

  not not_1 (not_1_out, in_1);
  xor xor_1 (in_4, in_1, in_2);
  and and_1 (and_1_out, not_1_out, in_2);
  not not_2 (not_2_out, in_4);
  xor xor_2 (in_3, in_4, undriven);
  and and_2 (and_2_out, not_2_out, undriven);
  or or_1 (in_5, and_2_out, and_1_out);
endmodule
