// Logisim project Half adder.circ as structural Verilog: 1 circuit, main circuit main
module main (
  output out_1,
  output out_2,
  output out_3,
  output out_4
);

  xor xor_1 (out_2, out_1, out_4);
  and \and  (out_3, out_1, out_4);
endmodule
